# Fritzing sketch CircuitDesign (saved by Fritzing 0.9.3b)
breadboards: 1

parts:
  Microcontroller = Arduino Uno (Rev3)
  XFW-H711 = HX711 Weighing Sensor Module
  S1 = Load Sensor - 50kg [part_number=SEN-10245]
  R2 = Resistor [tolerance=±5% resistance=220 package="2010 [SMD]"]
  R1 = Resistor [tolerance=±5% resistance=220 package="2010 [SMD]"]

nets:
  N1: Microcontroller.D2, XFW-H711.CK/TX
  N2: Microcontroller.D3_PWM, XFW-H711.DO/RX
  5V: Microcontroller.5V, XFW-H711.VCC
  GND: Microcontroller.GND, XFW-H711.GND
  N3: XFW-H711.E+, S1.W, R1.Pin_0
  N4: XFW-H711.E-, S1.B, R2.Pin_1
  N5: XFW-H711.A+, R2.Pin_0, R1.Pin_1
  N6: XFW-H711.A-, S1.R

custom parts:
  Load Sensor - 50kg: Half-wheatstone bridge Load Cell modified from the Fritzing Repo This load sensor, sometimes called a strain gauge, is the same one found in digital bathroom scales (you know, the ones you use in January for your New Year's resolutions, and then forget about a month later). This sensor can measure up to about 110 pounds.
